# Fritzing sketch Fritzing Design File (saved by Fritzing 0.9.3b)
circuit board: 8.46667cm x 5.64444cm
breadboards: 1

parts:
  Soil_Moisture_Sensor = Soil Moisture Sensor
  Arduino_Mega_2560 = Arduino Mega 2560 (Rev3)
  SRD-05VDC-SL-C_Relay = songle relay
  Amphibious_submersible_Micropump = DC Motor
  9V_DC_source = 9V Battery

nets:
  VCC: Soil_Moisture_Sensor.VCC, Arduino_Mega_2560.5V, SRD-05VDC-SL-C_Relay.VCC
  GND: Soil_Moisture_Sensor.GND, Arduino_Mega_2560.GND, SRD-05VDC-SL-C_Relay.GND
  N1: Soil_Moisture_Sensor.SIG, Arduino_Mega_2560.A0
  N2: Arduino_Mega_2560.D13_PWM, SRD-05VDC-SL-C_Relay.COMMON
  N3: SRD-05VDC-SL-C_Relay.NO, Amphibious_submersible_Micropump.pin_1, 9V_DC_source.+
  N4: SRD-05VDC-SL-C_Relay.NC, Amphibious_submersible_Micropump.pin_2, 9V_DC_source.-

custom parts:
  9V Battery: A nine volt battery

// code stored in the sketch: Untitled4.ino
//pins
int sensor_pin = A0;
int pump = 13;


int currentSoilMoistureLevel;

void setup() {
  // put your setup code here, to run once:
  pinMode(pump, OUTPUT);
  Serial.begin(9600);
  Serial.println("Running....");
  delay(2000);

}

void loop() {
  // put your main code here, to run repeatedly:
  currentSoilMoistureLevel = analogRead(sensor_pin);
  Serial.println("Moisture: ");
  Serial.println(currentSoilMoistureLevel);

  if (currentSoilMoistureLevel > 570){
    digitalWrite(pump,HIGH);
    
  } else if(currentSoilMoistureLevel < 220){
    digitalWrite(pump,LOW);  
    
  } else if((currentSoilMoistureLevel >= 220) || (currentSoilMoistureLevel <= 570)){
      float currentSoilMoistureLevelPercentage = (570 - currentSoilMoistureLevel);
      currentSoilMoistureLevelPercentage = currentSoilMoistureLevelPercentage * 100 / 350;
      Serial.println(currentSoilMoistureLevelPercentage);

      if(currentSoilMoistureLevelPercentage >= 50.0){ // If moisture level of 50% is required
        digitalWrite(pump,LOW);
      }else {
        digitalWrite(pump,HIGH);
      }
  
  }
  delay(1000);

}
